# Fritzing sketch scheme (saved by Fritzing 0.9.9b)
breadboards: 1

parts:
  WeMos_D1_Mini1 = WeMos D1 Mini
  U2 = 7-SEGMENT-4DIGIT [package=7-segment-4digit-youngsun]
  Part1 = Arduino Ethernet Shield (Rev3)
  U3 = POT [package=pot_alpha_rv16af-20]
  VCC1 = Battery block 9V  # not connected
  Driver1 = 28BYJ-48 Driver Module [part_number=ULN2003 package=THT]
  SM1 = 28BYJ-48 Stepper Motor [part_number=28BYJ-48]
  Part2 = Breadboard Power Supply Board SMD  # not connected

nets:
  N1: WeMos_D1_Mini1.5V, U3.E
  N2: WeMos_D1_Mini1.A0, U3.S
  N3: WeMos_D1_Mini1.D1, Part1.A5/SCL
  N4: WeMos_D1_Mini1.D2, Part1.A4/SDA
  N5: WeMos_D1_Mini1.D3, Driver1.IN1
  N6: WeMos_D1_Mini1.D4, Driver1.IN2
  N7: WeMos_D1_Mini1.D5, Driver1.IN3
  N8: WeMos_D1_Mini1.D6, Driver1.IN4
  N9: WeMos_D1_Mini1.G, U3.A
  N10: U2.1, Part1.PWM_D6
  N11: U2.2, Part1.PWM_D5
  N12: U2.3, Part1.PWM_D9
  N13: U2.4, Part1.SDCS
  N14: U2.6, Part1.D8
  N15: U2.8, Part1.ETH_CS
  N16: U2.9, Part1.PWM_D3
  N17: U2.11, Part1.SPI/D12
  N18: U2.13, Part1.PWM_D11
  N19: U2.14, Part1.D7
  N20: U2.15, Part1.D2
  N21: U2.16, Part1.SPI/D13
  N22: Driver1.blue-pin, SM1.blue-pin
  N23: Driver1.pink-pin, SM1.pink-pin
  N24: Driver1.yellow-pin, SM1.yellow-pin
  N25: Driver1.orange-pin, SM1.orange-pin
  N26: Driver1.red-pin, SM1.red-pin

custom parts:
  28BYJ-48 Driver Module: ULN2003 Driver Module for the 28BYJ-48 Unipolar Stepper Motor LED A - Blue wire - Bottom coil left LED B - Pink wire - Top coil left LED C - Yellow wire - Bottom coil right LED D - Orange wire - Top coil right Common rail - red Connector pins: blue - pink - yellow - orange - red Control pins - IN1 to IN4 Power pins - GND & Vmotor (5-12V) On/Off jumper (if removed, power to motor is cut).
  28BYJ-48 Stepper Motor: Unipolar Stepper Motor 28BYJ-48 Top coil - pink & orange Bottom coil - blue & yellow Common rail - red Connector pins: blue - pink - yellow - orange - red
